# Fritzing sketch vfobfo_atmega328_schematic (saved by Fritzing 0.9.3b)
breadboards: 1

parts:
  part = OLED Monochrome 128x64 0.96 inch [part_number=.]
  part_2 = Adafruit Si5351A Clock Generator [part_number=.]
  RE1 = Rotary Encoder [package=THT]
  R1 = Resistor [tolerance=±5% resistance=10k package="0805 [SMD]"]
  R2 = Resistor [tolerance=±5% resistance=10k package="0805 [SMD]"]
  R3 = Resistor [tolerance=±5% resistance=10k package="0805 [SMD]"]
  R5 = Resistor [tolerance=±5% resistance=10k package="0805 [SMD]"]
  R6 = Resistor [tolerance=±5% resistance=10k package="0805 [SMD]"]
  R7 = Resistor [tolerance=±5% resistance=10k package="0805 [SMD]"]
  C1 = Ceramic Capacitor [capacitance=10nF package="100 mil [THT, multilayer]"]
  S1 = SWITCH-MOMENTARY-2 [package=tactile-pth]
  S2 = SWITCH-MOMENTARY-2 [package=tactile-pth]
  S3 = SWITCH-MOMENTARY-2 [package=tactile-pth]
  part_3 = smd LED [color="Red (633nm)" package="0805 [SMD]"]
  R8 = Resistor [tolerance=±5% resistance=1k package="0805 [SMD]"]
  R4 = Resistor [tolerance=±5% resistance=10k package="0805 [SMD]"]
  part_4 = Arduino Pro Mini v13
  C2 = Ceramic Capacitor [capacitance=10nF package="100 mil [THT, multilayer]"]
  part_5 = TSOP312.., 314.. [package=THT]
  R9 = Resistor [tolerance=±5% resistance=1k package="0805 [SMD]"]

nets:
  N1: part.SCLK_SCK, part_2.SCL, part_4.A5
  N2: part.DC_SA0, part_2.SDA, part_4.A4
  5V: part.VIN, part_2.VIN, R6.Pin_1, R7.Pin_1, S3.2, part_4.VCC, part_4.D2, part_5.Vs
  GND: part.GND, part_2.GND, RE1.EncoderPinC, R3.Pin_0, R5.Pin_0, C1.0, R8.Pin_0, R4.Pin_0, part_4.GND, C2.1, R9.Pin_0
  N3: RE1.EncoderPinA, R2.Pin_1, R7.Pin_0
  N4: RE1.EncoderPinB, R1.Pin_1, R6.Pin_0
  N5: R1.Pin_0, C1.1, part_4.D6_PWM
  N6: R2.Pin_0, part_4.D5_PWM, C2.0
  N7: R3.Pin_1, S3.1
  N8: R5.Pin_1, S2.1
  N9: S1.1, R4.Pin_1
  N10: S1.2, part_4.D3_PWM
  N11: S2.2, part_4.D4
  N12: part_3.cathode, part_4.D13/SCK
  N13: part_3.anode, R8.Pin_1
  N14: part_4.D9_PWM, part_5.Data
  N15: part_5.GND, R9.Pin_1

notes:
  Band
  Step
  Switch VFO/BFO
  ENCODER
  C
  A
  B
  SLC
  SDA
  Si5351A
  OLED
  VFO and BFO with Si5351, OLED, IR and Arduino Atmega328
  By PU2CLR,
  April 15th, 2019
  IR
  LED
  D2
  D9
  D6
  D5
  D4
  D3

custom parts:
  OLED Monochrome 128x64 0.96 inch: These displays are small, only about 1" diameter, but very readable due to the high contrast of an OLED display. This display is made of 128x64 individual white OLED pixels, each one is turned on or off by the controller chip. Because the display makes its own light, no backlight is required. This reduces the power required to run the OLED and is why the display has such high contrast; we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
  Adafruit Si5351A Clock Generator: Never hunt around for another crystal again, with the Si5351A clock generator breakout from Adafruit! This chip has a precision 25MHz crystal reference and internal PLL and dividers so it can generate just about any frequency, from <8KHz up to 150+ MHz. The Si5351A clock generator is an I2C controller clock generator. It uses the onboard precision clock to drive multiple PLL's and clock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
