# Fritzing sketch coupling_02 (saved by Fritzing 0.9.3b)
breadboards: 1

parts:
  C1 = Ceramic Capacitor [capacitance=15pF package="200 mil [THT, multilayer]"]
  part = Adafruit Si5351A Clock Generator [part_number=.]
  R1 = Resistor [tolerance=±5% resistance=10M package="0603 [SMD]"]
  R2 = Resistor [tolerance=±5% resistance=220 package="0603 [SMD]"]
  CD2003GP = IC, DIP package, 16 pins [chip_label=IC]

nets:
  N1: C1.0, CD2003GP.pin13
  N2: C1.1, R1.Pin_1, R2.Pin_1
  5V: part.VIN
  GND: part.GND, R2.Pin_0
  N3: part.CLK0, R1.Pin_0

notes:
  Si5351A
  Coupling - Second test

custom parts:
  Adafruit Si5351A Clock Generator: Never hunt around for another crystal again, with the Si5351A clock generator breakout from Adafruit! This chip has a precision 25MHz crystal reference and internal PLL and dividers so it can generate just about any frequency, from <8KHz up to 150+ MHz. The Si5351A clock generator is an I2C controller clock generator. It uses the onboard precision clock to drive multiple PLL's and clock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
