# Fritzing sketch coupling_CD2003GP (saved by Fritzing 0.9.3b)
breadboards: 1

parts:
  part = Adafruit Si5351A Clock Generator [part_number=.]
  L1 = Inductor [package="0603 [SMD]"]
  L2 = Inductor [package="0603 [SMD]"]
  R1 = Resistor [tolerance=±5% resistance=220 package=THT]
  C1 = Ceramic Capacitor [capacitance=10n package="100 mil [THT, multilayer]"]
  C2 = Ceramic Capacitor [capacitance=15pF package="100 mil [THT, multilayer]"]
  CD2003GP = IC, DIP package, 16 pins [chip_label=IC]

nets:
  5V: part.VIN
  GND: part.GND, L1.pin_1, C1.0
  N1: part.CLK0, L1.pin_0
  N2: L2.pin_0, R1.Pin_1, C1.1
  N3: L2.pin_1, R1.Pin_0, C2.1
  N4: C2.0, CD2003GP.pin13

notes:
  Si5351A
  Coupling - Third test`

custom parts:
  Adafruit Si5351A Clock Generator: Never hunt around for another crystal again, with the Si5351A clock generator breakout from Adafruit! This chip has a precision 25MHz crystal reference and internal PLL and dividers so it can generate just about any frequency, from <8KHz up to 150+ MHz. The Si5351A clock generator is an I2C controller clock generator. It uses the onboard precision clock to drive multiple PLL's and clock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
