# Fritzing sketch vfobfo_schematic2 (saved by Fritzing 0.9.3b)
breadboards: 1

parts:
  ARDUINO1 = Arduino Micro
  OLED = OLED Monochrome 128x64 0.96 inch [part_number=.]
  Si5351A = Adafruit Si5351A Clock Generator [part_number=.]
  RE1 = Rotary Encoder [package=THT]
  R1 = Resistor [tolerance=±5% resistance=10k package="0805 [SMD]"]
  R2 = Resistor [tolerance=±5% resistance=10k package="0805 [SMD]"]
  R3 = Resistor [tolerance=±5% resistance=10k package="0805 [SMD]"]
  R4 = Resistor [tolerance=±5% resistance=10k package="0805 [SMD]"]
  R5 = Resistor [tolerance=±5% resistance=10k package="0805 [SMD]"]
  R6 = Resistor [tolerance=±5% resistance=10k package="0805 [SMD]"]
  R7 = Resistor [tolerance=±5% resistance=10k package="0805 [SMD]"]
  C1 = Ceramic Capacitor [capacitance=10nF package="100 mil [THT, multilayer]"]
  C2 = Ceramic Capacitor [capacitance=10nF package="100 mil [THT, multilayer]"]
  S1 = SWITCH-MOMENTARY-2 [package=tactile-pth]
  S2 = SWITCH-MOMENTARY-2 [package=tactile-pth]
  S3 = SWITCH-MOMENTARY-2 [package=tactile-pth]

nets:
  N1: ARDUINO1.TX, R5.Pin_0
  N2: ARDUINO1.RX, R4.Pin_0
  N3: ARDUINO1.D2, OLED.MOSI_SDA, Si5351A.SDA
  N4: ARDUINO1.D3, OLED.SCLK_SCK, Si5351A.SCL
  N5: ARDUINO1.D7, R3.Pin_0
  N6: ARDUINO1.D8, R2.Pin_0, C2.1
  N7: ARDUINO1.D9, R1.Pin_0, C1.0
  GND: ARDUINO1.GND, OLED.GND, Si5351A.GND, RE1.EncoderPinC, R3.Pin_1, R4.Pin_1, R5.Pin_1, C1.1, C2.0, S1.1, S2.1, S3.1
  5V: ARDUINO1.VIN, Si5351A.VIN, R6.Pin_1, R7.Pin_1, S1.2, S2.2, S3.2
  N8: RE1.EncoderPinA, R2.Pin_1, R7.Pin_0
  N9: RE1.EncoderPinB, R1.Pin_1, R6.Pin_0

notes:
  Band
  Step
  Switch VFO/BFO
  Encoder
  C
  A
  B
  SLC
  SDA

custom parts:
  Arduino Micro: Arduino Micro Microcontroller
  OLED Monochrome 128x64 0.96 inch: These displays are small, only about 1" diameter, but very readable due to the high contrast of an OLED display. This display is made of 128x64 individual white OLED pixels, each one is turned on or off by the controller chip. Because the display makes its own light, no backlight is required. This reduces the power required to run the OLED and is why the display has such high contrast; we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
  Adafruit Si5351A Clock Generator: Never hunt around for another crystal again, with the Si5351A clock generator breakout from Adafruit! This chip has a precision 25MHz crystal reference and internal PLL and dividers so it can generate just about any frequency, from <8KHz up to 150+ MHz. The Si5351A clock generator is an I2C controller clock generator. It uses the onboard precision clock to drive multiple PLL's and clock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
