# Fritzing sketch vfobfo_schematic (saved by Fritzing 0.9.3b)
breadboards: 1

parts:
  Arduino1 = Arduino Mini (Rev5)  # not connected
  S1 = Momentary Switch [package=ksa_sealed_tac_switch]

nets:
  N1: S1.1, S1.2
  N2: S1.3, S1.4
